# Fritzing sketch wirklichkeitssteuerungsgeraet (saved by Fritzing 0.9.3b)
breadboards: 1

parts:
  Bauteil1 = Arduino Nano (Rev3.0) (ICSP)
  GY1 = MPU-6050 Board GY-521 [form="♀ (female)" package=THT]
  X1 = DB9 Connector [package=db9]
  U1 = MCP2515 CAN Bus Module
  JP1 = Header 6 [package=1x06_smd_straight]

nets:
  GND: Bauteil1.GND, GY1.pin2, X1.2, U1.GND, JP1.6
  N1: Bauteil1.D2, U1.INT
  N2: Bauteil1.D3, GY1.pin8
  N3: Bauteil1.D4, X1.8
  N4: Bauteil1.D5, X1.7
  N5: Bauteil1.D6, X1.6
  N6: Bauteil1.D7, X1.5
  N7: Bauteil1.D8, X1.4
  N8: Bauteil1.D9, U1.CS
  N9: Bauteil1.D11/MOSI, U1.MOSI
  N10: Bauteil1.D12/MISO, U1.MISO
  N11: Bauteil1.VIN, JP1.4
  5V: Bauteil1.5V, GY1.pin1, U1.VCC
  N12: Bauteil1.A5, GY1.pin3
  N13: Bauteil1.A4, GY1.pin4
  N14: Bauteil1.D13/SCK, U1.SCK

custom parts:
  MPU-6050 Board GY-521: Acelerometro y Giroscopio MPU-6050 Board GY-521
  MCP2515 CAN Bus Module: MCP 2515 CAN Bus Module
